// Logisim project TinyCPU-Peripherals.circ as structural Verilog: 4 circuits, main circuit TinyCPUSystemMain
module TinyCPUSystemMain (
  input  CLK,
  input  RESET,
  input  INTERRUPT_REQUEST,
  output [15:0] OUTPUT_PORT_VALUE,
  output OUTPUT_PORT_VALID,
  output INTERRUPT_ENABLED,
  output INTERRUPT_PENDING,
  output IN_INTERRUPT_HANDLER,
  output [11:0] RETURN_ADDRESS,
  output RETURN_ADDRESS_VALID
);
endmodule

module OutputPort (
  input  [15:0] WRITE_VALUE,
  input  WRITE_VALID,
  input  WRITE_ENABLE,
  input  CLK,
  input  RESET,
  output [15:0] VALUE,
  output VALID
);

  Register #(.width(16)) OUTPUT_VALUE (.D(WRITE_VALUE), .en(WRITE_ENABLE), .clk(CLK), .Q(VALUE), .clr(RESET));
  Register #(.width(1)) OUTPUT_VALID (.D(WRITE_VALID), .en(WRITE_ENABLE), .clk(CLK), .Q(VALID), .clr(RESET));
endmodule

module OutputMemoryPath (
  input  [11:0] ADDRESS,
  input  [15:0] WRITE_VALUE,
  input  WRITE_VALID,
  input  WRITE_ENABLE,
  input  [15:0] RAM_READ_VALUE,
  input  RAM_READ_VALID,
  input  CLK,
  input  RESET,
  output [15:0] READ_VALUE,
  output READ_VALID,
  output RAM_WRITE_ENABLE,
  output [15:0] OUTPUT_PORT_VALUE,
  output OUTPUT_PORT_VALID
);

  wire NOT_OUTPUT_ADDRESS_out, OUTPUT_WRITE_GATE_out, RAM_WRITE_GATE_p2, RAM_WRITE_GATE_p4,
       RAM_WRITE_GATE_p6, undriven_2, undriven_3, undriven_4;
  wire [11:0] undriven;

  Comparator #(.width(12)) OUTPUT_ADDRESS_DECODE (.a(undriven), .b(ADDRESS));  // open: gt, eq, lt
  not NOT_OUTPUT_ADDRESS (NOT_OUTPUT_ADDRESS_out, undriven_2);
  // AND_Gate RAM_WRITE_GATE: pin names not known; wires that end beside it: WRITE_ENABLE, RAM_WRITE_GATE_p2, NOT_OUTPUT_ADDRESS_out, RAM_WRITE_GATE_p4, RAM_WRITE_GATE_p4, RAM_WRITE_GATE_p6, RAM_WRITE_ENABLE
  buf OUTPUT_WRITE_GATE (OUTPUT_WRITE_GATE_out, RAM_WRITE_GATE_p2);  // AND_Gate
  Multiplexer #(.width(16)) OUTPUT_READ_VALUE_SELECT (
    .in0(RAM_READ_VALUE), .in1(OUTPUT_PORT_VALUE), .out(READ_VALUE));  // open: sel
  Multiplexer OUTPUT_READ_VALID_SELECT (.in0(RAM_READ_VALID), .in1(OUTPUT_PORT_VALID), .out(READ_VALID));  // open: sel
  Register #(.width(16)) u_OUTPUT_PORT_VALUE (
    .D(WRITE_VALUE), .clk(undriven_3), .Q(OUTPUT_PORT_VALUE), .clr(undriven_4));  // open: en
  Register #(.width(1)) u_OUTPUT_PORT_VALID (
    .D(WRITE_VALID), .en(OUTPUT_WRITE_GATE_out), .clk(undriven_3), .Q(OUTPUT_PORT_VALID), .clr(undriven_4));
endmodule

module InterruptController (
  input  INTERRUPT_REQUEST,
  input  INSTRUCTION_BOUNDARY,
  input  ENABLE_REQUEST,
  input  DISABLE_REQUEST,
  input  RETURN_REQUEST,
  input  [11:0] NEXT_PC,
  input  CLK,
  input  RESET,
  output INTERRUPT_ACCEPT,
  output [11:0] TARGET_PC,
  output INTERRUPT_ENABLED,
  output INTERRUPT_PENDING,
  output IN_INTERRUPT_HANDLER,
  output [11:0] RETURN_ADDRESS,
  output RETURN_ADDRESS_VALID,
  output ILLEGAL_RETURN
);

  wire HANDLER_HOLD_out, HANDLER_NEXT_out, INTERRUPT_ACCEPT_GATE_p1, INTERRUPT_ACCEPT_GATE_p3,
       INTERRUPT_ENABLED_p2, INTERRUPT_PENDING_q, MASK_CLEAR_NOT_out, MASK_CLEAR_REQUEST_out,
       PENDING_HOLD_UNTIL_ACCEPT_p1, PREVIOUS_REQUEST_NOT_out, REQUEST_LEVEL_p1, REQUEST_LEVEL_p6,
       RETURN_ADDRESS_p2, RETURN_VALID_HOLD_out, RETURN_VALID_NEXT_p2, RETURN_VALID_NEXT_p3,
       RISING_EDGE_DETECT_out, undriven, undriven_2, undriven_3, undriven_5, VALID_RETURN_GATE_out,
       VALID_RETURN_NOT_out;
  wire [11:0] undriven_4;

  // OR_Gate PENDING_SET_OR_HOLD is placed but not wired
  // Register #(.width(12)) RETURN_ADDRESS: pin names not known; wires that end beside it: NEXT_PC, RETURN_ADDRESS_p2
  // Register #(.width(1)) RETURN_ADDRESS_VALID: pin names not known; wires that end beside it: RETURN_ADDRESS_p2, 1'b1, RETURN_ADDRESS_p2
  // OR_Gate MASK_SET_REQUEST is placed but not wired
  // OR_Gate MASK_CLEAR_REQUEST has open pins: out=MASK_CLEAR_REQUEST_out
  // Register #(.width(1)) REQUEST_LEVEL: pin names not known; wires that end beside it: REQUEST_LEVEL_p1, INTERRUPT_REQUEST, 1'b1, REQUEST_LEVEL_p1, 1'b1, REQUEST_LEVEL_p6
  // Register #(.width(1)) INTERRUPT_ENABLED: pin names not known; wires that end beside it: 1'b1, INTERRUPT_ENABLED_p2
  Register #(.width(1)) u_INTERRUPT_PENDING (.Q(INTERRUPT_PENDING_q));  // open: D, en, clk, clr
  Register #(.width(1)) u_IN_INTERRUPT_HANDLER (.en(CLK), .clr(undriven));  // open: D, clk, Q
  not MASK_CLEAR_NOT (MASK_CLEAR_NOT_out, MASK_CLEAR_REQUEST_out);
  not PREVIOUS_REQUEST_NOT (PREVIOUS_REQUEST_NOT_out, REQUEST_LEVEL_p6);
  // NOT_Gate NOT_IN_HANDLER has open pins: in=INTERRUPT_ENABLED_p2, out=open
  // AND_Gate MASK_HOLD has open pins: in0=undriven, in1=MASK_CLEAR_NOT_out, out=open
  and RISING_EDGE_DETECT (RISING_EDGE_DETECT_out, INTERRUPT_REQUEST, PREVIOUS_REQUEST_NOT_out);
  // AND_Gate INTERRUPT_ACCEPT_GATE: pin names not known; wires that end beside it: INTERRUPT_ACCEPT_GATE_p1, INTERRUPT_ACCEPT_GATE_p1, INTERRUPT_ACCEPT_GATE_p3
  // AND_Gate ILLEGAL_RETURN_GATE is placed but not wired
  // AND_Gate PENDING_HOLD_UNTIL_ACCEPT: pin names not known; wires that end beside it: PENDING_HOLD_UNTIL_ACCEPT_p1, PENDING_HOLD_UNTIL_ACCEPT_p1
  and VALID_RETURN_GATE (VALID_RETURN_GATE_out, RETURN_REQUEST, undriven_3, undriven_2);
  and RETURN_VALID_HOLD (RETURN_VALID_HOLD_out, undriven_2, VALID_RETURN_NOT_out);
  and HANDLER_HOLD (HANDLER_HOLD_out, undriven_3, VALID_RETURN_NOT_out);
  // NOT_Gate INTERRUPT_ACCEPT_NOT has open pins: in=INTERRUPT_ACCEPT_GATE_p3, out=open
  Multiplexer #(.width(12)) INTERRUPT_TARGET_SELECT (.in0(12'hff0), .in1(undriven_4), .sel(undriven_5));  // open: out
  // OR_Gate MASK_NEXT is placed but not wired
  not VALID_RETURN_NOT (VALID_RETURN_NOT_out, VALID_RETURN_GATE_out);
  // OR_Gate HANDLER_NEXT has open pins: out=HANDLER_NEXT_out
  // OR_Gate RETURN_VALID_NEXT: pin names not known; wires that end beside it: RETURN_VALID_HOLD_out, RETURN_VALID_NEXT_p2, RETURN_VALID_NEXT_p3

  // Notes on the sheet:
  //   MASK NEXT STATE
  //   AP-18 interrupt state: reset > accept at instruction boundary > instruction; rising edges remain pending while masked
  //   RETURN VALID NEXT STATE
  //   HANDLER NEXT STATE
endmodule
