// Logisim project TinyCPU.circ as structural Verilog: 21 circuits, main circuit TinyCPUMain
module TinyCPUMain (
  input  CLK,
  input  RESET,
  output [15:0] PRINT_VALUE,
  output PRINT_ADDRESS_VALID,
  output [15:0] PRINT_ADDRESS_VALUE,
  output PRINT_VALID,
  output ERROR_OVF,
  output ERROR_DIV0,
  output ERROR_ADDR,
  output ERROR_INV,
  output ERROR_ILL,
  output ERROR_INPUT,
  output PRINT_ENABLE,
  output PRINT_ADDRESS_ENABLE,
  output HALTED,
  output HALTED_WITH_ERROR
);

  wire ANY_ERROR_CONDITION, ANY_JUMP_CONDITION, ANY_JUMP_CONTROL, ERROR_ADDR_CONDITION, ERROR_DIV0_CONDITION,
       ERROR_ILL_CONDITION, ERROR_INPUT_CONDITION, ERROR_INV_CONDITION, ERROR_OVF_CONDITION,
       FETCH_DECODE_2_p3, FETCH_DECODE_CONTROLS_p5, FETCH_DECODE_CONTROLS_p6, FETCH_DECODE_CONTROLS_p7,
       FETCH_DECODE_CONTROLS_p8, FETCH_DECODE_CONTROLS_p9, FETCH_DECODE_CONTROLS_p10,
       FETCH_DECODE_CONTROLS_p11, FETCH_DECODE_CONTROLS_p12, FETCH_DECODE_CONTROLS_p13,
       FETCH_DECODE_CONTROLS_p14, FETCH_DECODE_CONTROLS_p15, FETCH_DECODE_CONTROLS_p16,
       FETCH_DECODE_CONTROLS_p17, FETCH_DECODE_halt_error, FETCH_DECODE_jump_not_zero, JUMP_ADR_CONTROL,
       JUMP_ADR_OR_JNZ_CONTROL_RESULT, JUMP_ADR_OR_JNZ_TAKEN, JUMP_ERROR_CONTROL,
       JUMP_ERROR_OR_PREVIOUS_CONTROLS_RESULT, JUMP_ERROR_OR_PREVIOUS_TAKEN_RESULT, JUMP_ERROR_TAKEN,
       JUMP_NEGATIVE_CONTROL, JUMP_NEGATIVE_OR_PREVIOUS_CONTROLS_RESULT,
       JUMP_NEGATIVE_OR_PREVIOUS_TAKEN_RESULT, JUMP_NEGATIVE_TAKEN, JUMP_NOT_ERROR_CONTROL,
       JUMP_NOT_ERROR_TAKEN, JUMP_ZERO_CONTROL, JUMP_ZERO_OR_PREVIOUS_CONTROLS_RESULT,
       JUMP_ZERO_OR_PREVIOUS_TAKEN_RESULT, JUMP_ZERO_TAKEN, MEMORY_INSTANCE_memory_valid,
       MEMORY_WRITE_REQUEST_out, NO_ERROR_CONDITION, NOT_ZERO_CONDITION, OPERATIONS_INSTANCE_p1,
       OPERATIONS_INSTANCE_p2, undriven, undriven_2, undriven_3, undriven_4, undriven_6, undriven_9,
       undriven_11, ZERO_CONDITION;
  wire [11:0] FETCH_DECODE_pc_out;
  wire [15:0] MEMORY_INSTANCE_memory_data, multiplexer_1_out, undriven_5, undriven_7, undriven_8, undriven_10;
  wire [21:0] FETCH_DECODE_opcode;

  or MEMORY_WRITE_REQUEST (MEMORY_WRITE_REQUEST_out, undriven_4, undriven_3, FETCH_DECODE_CONTROLS_p16);
  // OR_Gate MEMORY_WRITE_REQUEST_2 is placed but not wired
  // OR_Gate JUMP_ADR_OR_JNZ_CONTROL has open pins: out=JUMP_ADR_OR_JNZ_CONTROL_RESULT
  // OR_Gate JUMP_ADR_OR_NOT_ZERO has open pins: out=JUMP_ADR_OR_JNZ_TAKEN
  // AND_Gate JUMP_ZERO_AND_ZERO has open pins: out=JUMP_ZERO_TAKEN
  // OR_Gate JUMP_ZERO_OR_PREVIOUS_CONTROLS has open pins: out=JUMP_ZERO_OR_PREVIOUS_CONTROLS_RESULT
  // OR_Gate JUMP_ZERO_OR_PREVIOUS_TAKEN has open pins: out=JUMP_ZERO_OR_PREVIOUS_TAKEN_RESULT
  FetchDecode FETCH_DECODE (
    .CLK(undriven), .RESET(undriven_2), .DEC_JUMP_NOT_ZERO(ANY_JUMP_CONTROL), .NOT_ZERO(ANY_JUMP_CONDITION),
    .PROGRAM_LIMIT(undriven_8), .DEC_HALT_ERROR(undriven_9), .JUMP_NOT_ZERO(FETCH_DECODE_jump_not_zero),
    .HALT_ERROR(FETCH_DECODE_halt_error), .PC_OUT(FETCH_DECODE_pc_out), .OPCODE(FETCH_DECODE_opcode));
  Memory MEMORY_INSTANCE (
    .ADDRESS(undriven_7), .WRITE_ENABLE(MEMORY_WRITE_REQUEST_out), .CLK(undriven), .VALID_IN(undriven_6),
    .DATA_IN(undriven_5), .MEMORY_VALID(MEMORY_INSTANCE_memory_valid),
    .MEMORY_DATA(MEMORY_INSTANCE_memory_data));
  // AND_Gate JUMP_NEGATIVE_AND_NEGATIVE has open pins: out=JUMP_NEGATIVE_TAKEN
  // FetchDecode FETCH_DECODE_2: pin names not known; wires that end beside it: 16'hfff, 1'b1, FETCH_DECODE_2_p3, FETCH_DECODE_2_p3
  Memory MEMORY_INSTANCE_2 ();  // open: ADDRESS, WRITE_ENABLE, CLK, VALID_IN, DATA_IN, MEMORY_VALID, MEMORY_DATA
  // OR_Gate JUMP_NEGATIVE_OR_PREVIOUS_CONTROLS has open pins: out=JUMP_NEGATIVE_OR_PREVIOUS_CONTROLS_RESULT
  // OR_Gate JUMP_NEGATIVE_OR_PREVIOUS_TAKEN has open pins: out=JUMP_NEGATIVE_OR_PREVIOUS_TAKEN_RESULT
  // Probe on nothing
  // Probe on nothing
  // Probe on nothing
  // AND_Gate JUMP_ERROR_AND_ANY_ERROR has open pins: out=JUMP_ERROR_TAKEN
  or ANY_ERROR_FLAG (ANY_ERROR_CONDITION, ERROR_OVF_CONDITION, ERROR_DIV0_CONDITION, ERROR_ADDR_CONDITION, ERROR_INV_CONDITION, ERROR_ILL_CONDITION, ERROR_INPUT_CONDITION);
  // OR_Gate JUMP_ERROR_OR_PREVIOUS_CONTROLS has open pins: out=JUMP_ERROR_OR_PREVIOUS_CONTROLS_RESULT
  // OR_Gate JUMP_ERROR_OR_PREVIOUS_TAKEN has open pins: out=JUMP_ERROR_OR_PREVIOUS_TAKEN_RESULT
  // AddressPath ADDRESS_PATH: pin names not known; wires that end beside it: 16'h1, 16'h1, 1'b1, 1'b1
  // FetchDecodeControls FETCH_DECODE_CONTROLS: pin names not known; wires that end beside it: JUMP_NEGATIVE_OR_PREVIOUS_CONTROLS_RESULT, JUMP_ERROR_CONTROL, JUMP_NEGATIVE_OR_PREVIOUS_TAKEN_RESULT, JUMP_ERROR_TAKEN, FETCH_DECODE_CONTROLS_p5, FETCH_DECODE_CONTROLS_p6, FETCH_DECODE_CONTROLS_p7, FETCH_DECODE_CONTROLS_p8, FETCH_DECODE_CONTROLS_p9, FETCH_DECODE_CONTROLS_p10, FETCH_DECODE_CONTROLS_p11, FETCH_DECODE_CONTROLS_p12, FETCH_DECODE_CONTROLS_p13, FETCH_DECODE_CONTROLS_p14, FETCH_DECODE_CONTROLS_p15, FETCH_DECODE_CONTROLS_p16, FETCH_DECODE_CONTROLS_p17, JUMP_ADR_CONTROL, JUMP_ZERO_CONTROL, JUMP_NEGATIVE_CONTROL, JUMP_ERROR_CONTROL, JUMP_NOT_ERROR_CONTROL, FETCH_DECODE_CONTROLS_p11, FETCH_DECODE_CONTROLS_p12, FETCH_DECODE_CONTROLS_p13, FETCH_DECODE_CONTROLS_p14
  // Probe on nothing
  // Probe on nothing
  // Probe on nothing
  // Probe on nothing
  // Probe on nothing
  // Probe on nothing
  // Probe on nothing
  // Probe on nothing
  // Probe on nothing
  not INVERT_ZERO_FOR_JNZ (NOT_ZERO_CONDITION, ZERO_CONDITION);
  // Datapath DATAPATH_INSTANCE: pin names not known; wires that end beside it: 1'b0
  Multiplexer #(.width(16)) multiplexer_1 (
    .in0(undriven_10), .in1(MEMORY_INSTANCE_memory_data), .out(multiplexer_1_out), .sel(undriven_11));
  // ErrorFlags ERROR_FLAGS: pin names not known; wires that end beside it: ERROR_INPUT_CONDITION
  // Operations OPERATIONS_INSTANCE: pin names not known; wires that end beside it: OPERATIONS_INSTANCE_p1, OPERATIONS_INSTANCE_p2
  // EffectiveAddress EFFECTIVE_ADDRESS_FBOX: pin names not known
  // AddressRangeFBox ADDRESS_RANGE_FBOX: pin names not known
  // Probe on nothing
  // Probe on nothing
  // Probe on nothing
  // Probe on nothing
  // Probe on nothing
  // Probe on nothing
  // Probe on nothing
  // OR_Gate JUMP_NOT_ERROR_OR_PREVIOUS_CONTROLS has open pins: out=ANY_JUMP_CONTROL
  // NOT_Gate INVERT_ANY_ERROR_FOR_JUMP_NOT_ERROR has open pins: in=open, out=NO_ERROR_CONDITION
  // AND_Gate JUMP_NOT_ERROR_AND_NO_ERROR has open pins: out=JUMP_NOT_ERROR_TAKEN
  // OR_Gate JUMP_NOT_ERROR_OR_PREVIOUS_TAKEN has open pins: out=ANY_JUMP_CONDITION
endmodule

module EffectiveAddress (
  input  [15:0] DIRECT_ADDR,
  input  [15:0] REG_ADDR,
  input  ADDR_REG_ARGUMENT,
  input  [15:0] OFFSET_ADDR,
  input  [15:0] REG_SELECTED,
  input  ADDR_REG_OFFS_ARGUMENT,
  output [15:0] EFFECTIVE_REGISTER_SELECTED_OUT,
  output EFFECTIVE_REGISTER_MODE,
  output [15:0] EFFECTIVE_MEMORY_ADDRESS,
  output EFFECTIVE_OFFSET_MODE,
  output ADDRESS_OUT_OF_RANGE
);

  Multiplexer #(.width(16)) multiplexer_1 (
    .in0(DIRECT_ADDR), .in1(REG_ADDR), .out(EFFECTIVE_REGISTER_SELECTED_OUT), .sel(ADDR_REG_ARGUMENT));
  Multiplexer #(.width(16)) multiplexer_2 (
    .in0(REG_SELECTED), .in1(OFFSET_ADDR), .out(EFFECTIVE_MEMORY_ADDRESS), .sel(ADDR_REG_OFFS_ARGUMENT));
  Comparator #(.width(16)) comparator_1 (
    .a(EFFECTIVE_MEMORY_ADDRESS), .b(16'hfff), .gt(ADDRESS_OUT_OF_RANGE));  // open: eq, lt

  assign EFFECTIVE_OFFSET_MODE = ADDR_REG_OFFS_ARGUMENT;
  assign EFFECTIVE_REGISTER_MODE = ADDR_REG_ARGUMENT;
endmodule

module Datapath (
  input  [15:0] DATA_IN,
  input  DATAPATH_STARTUP_RESET,
  input  ACC_LOAD,
  input  VALID_IN,
  input  CLK,
  output [15:0] ACC_OUT,
  output ZERO,
  output NEGATIVE,
  output ACC_VALID_OUT
);

  Register #(.width(16)) ACC (.D(DATA_IN), .en(ACC_LOAD), .clk(CLK), .Q(ACC_OUT), .clr(DATAPATH_STARTUP_RESET));
  Register #(.width(1)) ACC_VALID (
    .D(VALID_IN), .en(ACC_LOAD), .clk(CLK), .Q(ACC_VALID_OUT), .clr(DATAPATH_STARTUP_RESET));
  Comparator #(.width(16)) comparator_1 (.a(ACC_OUT), .b({16{1'b0}}), .eq(ZERO), .lt(NEGATIVE));  // open: gt

  // Notes on the sheet:
  //   Clocked 16-bit accumulator; signed comparator derives ZERO and NEGATIVE
endmodule

module AddressPath (
  input  [15:0] ADDRESS_IN,
  input  AR_LOAD,
  input  [15:0] OFFSET,
  input  VALID_IN,
  input  CLK,
  input  ADDRESS_PATH_STARTUP_RESET,
  output [15:0] ADDRESS,
  output [15:0] ADDRESS_PLUS_OFFSET,
  output OFFSET_CARRY,
  output ADDRESS_VALID
);

  Register #(.width(16)) AR (.D(ADDRESS_IN), .en(AR_LOAD), .clk(CLK), .Q(ADDRESS), .clr(ADDRESS_PATH_STARTUP_RESET));
  Register #(.width(1)) AR_VALID (
    .D(VALID_IN), .en(AR_LOAD), .clk(CLK), .Q(ADDRESS_VALID), .clr(ADDRESS_PATH_STARTUP_RESET));
  Adder #(.width(16)) adder_1 (.a(ADDRESS), .b(OFFSET), .out(ADDRESS_PLUS_OFFSET), .cout(OFFSET_CARRY));  // open: cin

  // Notes on the sheet:
  //   Clocked 12-bit address register with combinational offset addition
endmodule

module Memory (
  input  [15:0] ADDRESS,
  input  WRITE_ENABLE,
  input  CLK,
  input  VALID_IN,
  input  [15:0] DATA_IN,
  output MEMORY_VALID,
  output [15:0] MEMORY_DATA
);

  RAM #(.addrWidth(12), .asyncread("true"), .dataWidth(1)) VALID_RAM (
    .addr(ADDRESS[11:0]), .we(WRITE_ENABLE), .oe(1'b1), .clk(CLK), .din(VALID_IN), .dout(MEMORY_VALID));
  RAM #(.addrWidth(12), .asyncread("true"), .dataWidth(16)) DATA_RAM (
    .addr(ADDRESS[11:0]), .we(WRITE_ENABLE), .oe(1'b1), .clk(CLK), .din(DATA_IN), .dout(MEMORY_DATA));

  // Notes on the sheet:
  //   4096-word value/valid memory with shared address, write-enable, and clock
endmodule

module ErrorFlags (
  input  CLEAR_ERROR,
  input  CLK,
  input  SET_OVF,
  input  SET_DIV0,
  input  SET_ADDR,
  input  SET_INV,
  input  SET_ILL,
  input  SET_INPUT,
  output OVF_OUT,
  output DIV0_OUT,
  output ADDR_OUT,
  output INV_OUT,
  output ILL_OUT,
  output INPUT_OUT
);

  wire HOLD_ADDR_out, HOLD_DIV0_out, HOLD_ILL_out, HOLD_INPUT_out, HOLD_INV_out, HOLD_OVF_out, NEXT_ADDR_out,
       NEXT_DIV0_out, NEXT_ILL_out, NEXT_INPUT_out, NEXT_INV_out, NEXT_OVF_out, NOT_CLEAR_ERROR_out;

  not NOT_CLEAR_ERROR (NOT_CLEAR_ERROR_out, CLEAR_ERROR);
  and HOLD_OVF (HOLD_OVF_out, OVF_OUT, NOT_CLEAR_ERROR_out);
  and HOLD_DIV0 (HOLD_DIV0_out, DIV0_OUT, NOT_CLEAR_ERROR_out);
  and HOLD_INV (HOLD_INV_out, INV_OUT, NOT_CLEAR_ERROR_out);
  or NEXT_DIV0 (NEXT_DIV0_out, SET_DIV0, HOLD_DIV0_out);
  and HOLD_ADDR (HOLD_ADDR_out, ADDR_OUT, NOT_CLEAR_ERROR_out);
  and HOLD_ILL (HOLD_ILL_out, ILL_OUT, NOT_CLEAR_ERROR_out);
  and HOLD_INPUT (HOLD_INPUT_out, INPUT_OUT, NOT_CLEAR_ERROR_out);
  or NEXT_OVF (NEXT_OVF_out, SET_OVF, HOLD_OVF_out);
  or NEXT_ADDR (NEXT_ADDR_out, SET_ADDR, HOLD_ADDR_out);
  or NEXT_INV (NEXT_INV_out, SET_INV, HOLD_INV_out);
  or NEXT_ILL (NEXT_ILL_out, SET_ILL, HOLD_ILL_out);
  or NEXT_INPUT (NEXT_INPUT_out, SET_INPUT, HOLD_INPUT_out);
  Register #(.width(1)) OVF (.D(NEXT_OVF_out), .en(1'b1), .clk(CLK), .Q(OVF_OUT), .clr(CLEAR_ERROR));
  Register #(.width(1)) DIV0 (.D(NEXT_DIV0_out), .en(1'b1), .clk(CLK), .Q(DIV0_OUT), .clr(CLEAR_ERROR));
  Register #(.width(1)) ADDR (.D(NEXT_ADDR_out), .en(1'b1), .clk(CLK), .Q(ADDR_OUT), .clr(CLEAR_ERROR));
  Register #(.width(1)) INV (.D(NEXT_INV_out), .en(1'b1), .clk(CLK), .Q(INV_OUT), .clr(CLEAR_ERROR));
  Register #(.width(1)) ILL (.D(NEXT_ILL_out), .en(1'b1), .clk(CLK), .Q(ILL_OUT), .clr(CLEAR_ERROR));
  Register #(.width(1)) INPUT (.D(NEXT_INPUT_out), .en(1'b1), .clk(CLK), .Q(INPUT_OUT), .clr(CLEAR_ERROR));

  // Notes on the sheet:
  //   Set-dominant sticky flags: SET OR (current AND NOT CLEAR_ERROR)
endmodule

module FetchDecode (
  input  CLK,
  input  RESET,
  input  DEC_JUMP_NOT_ZERO,
  input  NOT_ZERO,
  input  [15:0] PROGRAM_LIMIT,
  input  DEC_HALT_ERROR,
  output JUMP_NOT_ZERO,
  output HALT_ERROR,
  output [11:0] PC_OUT,
  output [21:0] OPCODE
);

  wire comparator_1_gt;
  wire [15:0] adder_1_out, multiplexer_1_out;
  wire [15:12] PC_q;

  Register #(.width(16)) PC (.D(multiplexer_1_out), .en(1'b1), .clk(CLK), .Q({PC_q, PC_OUT}), .clr(RESET));
  and JNZ_TAKEN (JUMP_NOT_ZERO, DEC_JUMP_NOT_ZERO, NOT_ZERO);
  Adder #(.width(16)) adder_1 (.a({PC_q, PC_OUT}), .b(16'h1), .out(adder_1_out));  // open: cin, cout
  Comparator #(.width(16)) comparator_1 (.a({PC_q, PC_OUT}), .b(PROGRAM_LIMIT), .gt(comparator_1_gt));  // open: eq, lt
  Multiplexer #(.width(16)) multiplexer_1 (
    .in0(adder_1_out), .in1(OPCODE[15:0]), .out(multiplexer_1_out), .sel(JUMP_NOT_ZERO));
  ROM #(.addrWidth(12), .dataWidth(22)) INSTRUCTION_ROM (.addr(PC_OUT), .data(OPCODE));
  or ERROR_HALT (HALT_ERROR, comparator_1_gt, DEC_HALT_ERROR);

  // Notes on the sheet:
  //   PROGRAM_LIMIT: initial=0xfff
  //   AP 7 machine format v1: stable six-bit opcode allocation and encoder-generated ROM
  //   contents of INSTRUCTION_ROM (hex, n*v repeats v):
  //   ffff 1c0065 3 1c0064 2a0000 4ffff 1c0064 240004 2c0000
endmodule

module FetchDecodeControls (
  input  [5:0] OPCODE,
  output ADD_OPERAND,
  output SUB_OPERAND,
  output MUL_OPERAND,
  output DIV_OPERAND,
  output AND_OPERAND,
  output OR_OPERAND,
  output XOR_OPERAND,
  output CONST_ARGUMENT,
  output ADDR_ARGUMENT,
  output ADDR_REG_ARGUMENT,
  output ADDR_REG_OFFS_ARGUMENT,
  output NOT,
  output JUMP_ADR,
  output JUMP_ZERO,
  output JUMP_NOT_ZERO,
  output JUMP_NEGATIVE,
  output JUMP_ERROR,
  output JUMP_NOT_ERROR,
  output LOAD_CONST,
  output LOAD_ADR,
  output LOAD_ADR_REG,
  output LOAD_REG_OFF,
  output LD_REG_CONST,
  output LD_REG_ADR,
  output STORE_ADR,
  output STORE_ADR_REG,
  output STORE_REG_OFF,
  output SET_OVF,
  output SET_DIV0,
  output SET_ADDR,
  output SET_INV,
  output SET_ILL,
  output SET_INPUT,
  output CLEAR_ERROR,
  output INPUT,
  output PRINT,
  output PRINT_ADR,
  output HALT,
  output HALT_ERROR,
  output INVALID_OPERAND,
  output ACC_MEMORY_REQUEST,
  output ACC_WRITE_REQUEST
);

  wire decoder_1_out0, decoder_1_out1, decoder_1_out2, decoder_1_out3, decoder_1_out4, decoder_1_out5,
       decoder_1_out6, decoder_1_out7, decoder_1_out8, decoder_1_out9, decoder_1_out10, decoder_1_out11,
       decoder_1_out12, decoder_1_out13, decoder_1_out14, decoder_1_out15, decoder_1_out16, decoder_1_out17,
       decoder_1_out18, decoder_1_out19, decoder_1_out20, decoder_1_out21, decoder_1_out22, decoder_1_out23,
       decoder_1_out24, decoder_1_out25, decoder_1_out26, decoder_1_out27, decoder_1_out56, decoder_1_out57,
       decoder_1_out58, decoder_1_out59, decoder_1_out60, decoder_1_out61, decoder_1_out62, decoder_1_out63;

  Decoder #(.select(6)) decoder_1 (
    .out0(decoder_1_out0), .out1(decoder_1_out1), .out2(decoder_1_out2), .out3(decoder_1_out3),
    .out4(decoder_1_out4), .out5(decoder_1_out5), .out6(decoder_1_out6), .out7(decoder_1_out7),
    .out8(decoder_1_out8), .out9(decoder_1_out9), .out10(decoder_1_out10), .out11(decoder_1_out11),
    .out12(decoder_1_out12), .out13(decoder_1_out13), .out14(decoder_1_out14), .out15(decoder_1_out15),
    .out16(decoder_1_out16), .out17(decoder_1_out17), .out18(decoder_1_out18), .out19(decoder_1_out19),
    .out20(decoder_1_out20), .out21(decoder_1_out21), .out22(decoder_1_out22), .out23(decoder_1_out23),
    .out24(decoder_1_out24), .out25(decoder_1_out25), .out26(decoder_1_out26), .out27(decoder_1_out27),
    .out28(NOT), .out29(JUMP_ADR), .out30(JUMP_ZERO), .out31(JUMP_NOT_ZERO), .out32(JUMP_NEGATIVE),
    .out33(JUMP_ERROR), .out34(JUMP_NOT_ERROR), .out35(LOAD_CONST), .out36(LOAD_ADR), .out37(LOAD_ADR_REG),
    .out38(LOAD_REG_OFF), .out39(LD_REG_CONST), .out40(LD_REG_ADR), .out41(STORE_ADR), .out42(STORE_ADR_REG),
    .out43(STORE_REG_OFF), .out44(SET_OVF), .out45(SET_DIV0), .out46(SET_ADDR), .out47(SET_INV),
    .out48(SET_ILL), .out49(SET_INPUT), .out50(CLEAR_ERROR), .out51(INPUT), .out52(PRINT), .out53(PRINT_ADR),
    .out54(HALT), .out55(HALT_ERROR), .out56(decoder_1_out56), .out57(decoder_1_out57),
    .out58(decoder_1_out58), .out59(decoder_1_out59), .out60(decoder_1_out60), .out61(decoder_1_out61),
    .out62(decoder_1_out62), .out63(decoder_1_out63), .sel(OPCODE));  // open: en
  or ADD_OPERAND_SELECT (ADD_OPERAND, decoder_1_out0, decoder_1_out1, decoder_1_out2, decoder_1_out3);
  or SUB_OPERAND_SELECT (SUB_OPERAND, decoder_1_out4, decoder_1_out5, decoder_1_out6, decoder_1_out7);
  or MUL_OPERAND_SELECT (MUL_OPERAND, decoder_1_out8, decoder_1_out9, decoder_1_out10, decoder_1_out11);
  or DIV_OPERAND_SELECT (DIV_OPERAND, decoder_1_out12, decoder_1_out13, decoder_1_out14, decoder_1_out15);
  or AND_OPERAND_SELECT (AND_OPERAND, decoder_1_out16, decoder_1_out17, decoder_1_out18, decoder_1_out19);
  or OR_OPERAND_SELECT (OR_OPERAND, decoder_1_out20, decoder_1_out21, decoder_1_out22, decoder_1_out23);
  or XOR_OPERAND_SELECT (XOR_OPERAND, decoder_1_out24, decoder_1_out25, decoder_1_out26, decoder_1_out27);
  or CONST_ARUGMENT_SELECT (CONST_ARGUMENT, decoder_1_out0, decoder_1_out4, decoder_1_out8, decoder_1_out12, decoder_1_out16, decoder_1_out20, decoder_1_out24);
  or ADDR_ARGUM_SELECT (ADDR_ARGUMENT, decoder_1_out1, decoder_1_out5, decoder_1_out9, decoder_1_out13, decoder_1_out17, decoder_1_out21, decoder_1_out25);
  or ADDR_REG_ARGUMENT_SELECT (ADDR_REG_ARGUMENT, decoder_1_out2, decoder_1_out6, decoder_1_out10, decoder_1_out14, decoder_1_out18, decoder_1_out22, decoder_1_out26);
  or ADDR_REG_OFFS_ARGUMENT_SELECGT (ADDR_REG_OFFS_ARGUMENT, decoder_1_out3, decoder_1_out7, decoder_1_out11, decoder_1_out15, decoder_1_out19, decoder_1_out23, decoder_1_out27);
  or INVALID_OPERAND_SELECT (INVALID_OPERAND, decoder_1_out56, decoder_1_out57, decoder_1_out58, decoder_1_out59, decoder_1_out60, decoder_1_out61, decoder_1_out62, decoder_1_out63);
  or ACC_MEMORY_SELECT (ACC_MEMORY_REQUEST, LD_REG_ADR, STORE_ADR, STORE_ADR_REG);
  or ACC_LOAD_REQUEST (ACC_WRITE_REQUEST, ADD_OPERAND, SUB_OPERAND, MUL_OPERAND, DIV_OPERAND, AND_OPERAND, OR_OPERAND, XOR_OPERAND, NOT, LOAD_CONST, LOAD_ADR, LOAD_ADR_REG, LOAD_REG_OFF, LD_REG_CONST, LD_REG_ADR, STORE_ADR, STORE_ADR_REG, STORE_REG_OFF, CLEAR_ERROR);

  // Notes on the sheet:
  //   NOT: invertiert den Akkumulator bitweise
  //   PRINT: gibt den Akkumulator aus
  //   HALT: hält die CPU regulär an
  //   JUMP_ADR: springt unbedingt zur Adresse
  //   SET_OVF: setzt den Überlauffehler
  //   SET_DIV0: setzt den Fehler Division durch null
  //   SET_ADDR: setzt den Adressfehler
  //   SET_INV: setzt den Ungültigkeitsfehler
  //   SET_ILL: setzt den Fehler für unbekannte Befehle
  //   SET_INPUT: setzt den Eingabefehler
  //   INPUT: liest einen Wert in den Akkumulator
  //   HALT_ERROR: hält die CPU mit Fehler an
  //   ADD_OPERAND: addiert den gewählten Operanden
  //   SUB_OPERAND: subtrahiert den gewählten Operanden
  //   DIV_OPERAND: dividiert durch den gewählten Operanden
  //   JUMP_ZERO: springt, wenn der Akkumulator null ist
  //   JUMP_ERROR: springt, wenn ein Fehler gesetzt ist
  //   LOAD_CONST: lädt die Konstante in den Akkumulator
  //   LOAD_ADR: lädt den Speicherwert an der Adresse
  //   LD_REG_CONST: lädt die Konstante in das Adressregister
  //   LD_REG_ADR: lädt das Adressregister aus der Speicheradresse
  //   STORE_ADR: speichert den Akkumulator an der Adresse
  //   CLEAR_ERROR: löscht alle Fehlermerker
  //   PRINT_ADR: gibt den Speicherwert an der Adresse aus
  //   MUL_OPERAND: multipliziert mit dem gewählten Operanden
  //   AND_OPERAND: bitweises UND mit dem gewählten Operanden
  //   OR_OPERAND: bitweises ODER mit dem gewählten Operanden
  //   XOR_OPERAND: bitweises XOR mit dem gewählten Operanden
  //   CONST_ARGUMENT: verwendet die Konstante als Argument
  //   ADDR_ARGUMENT: verwendet den Speicherwert an der Adresse
  //   JUMP_NOT_ZERO: springt, wenn der Akkumulator nicht null ist
  //   JUMP_NEGATIVE: springt, wenn der Akkumulator negativ ist
  //   JUMP_NOT_ERROR: springt, wenn kein Fehler gesetzt ist
  //   LOAD_ADR_REG: lädt den Speicherwert am Adressregister
  //   LOAD_REG_OFF: lädt den Speicherwert bei Adressregister plus Offset
  //   STORE_ADR_REG: speichert den Akkumulator am Adressregister
  //   STORE_REG_OFF: speichert den Akkumulator bei Adressregister plus Offset
  //   INVALID_OPERAND: meldet einen reservierten Opcode als ungültig
  //   ADDR_REG_ARGUMENT: verwendet den Speicherwert am Adressregister
  //   ACC_MEMORY_REQUEST: fordert einen Speicherwert für den Akkumulator an
  //   ACC_WRITE_REQUEST: schreibt das Operationsergebnis in den Akkumulator
  //   ADDR_REG_OFFS_ARGUMENT: verwendet den Speicherwert bei Adressregister plus Offset
endmodule

module IntegrationClock (
  input  CLK,
  output FETCH_CLK,
  output DATAPATH_CLK,
  output ADDRESS_CLK,
  output MEMORY_CLK,
  output ERROR_FLAGS_CLK
);


  assign ADDRESS_CLK = CLK;
  assign DATAPATH_CLK = CLK;
  assign ERROR_FLAGS_CLK = CLK;
  assign FETCH_CLK = CLK;
  assign MEMORY_CLK = CLK;
endmodule

module IntegrationReset (
  input  RESET,
  output FETCH_RESET
);


  assign FETCH_RESET = RESET;
endmodule

module AndArithmeticCircuit (
  input  AND_ACTIVATED,
  input  [15:0] LEFT,
  input  [15:0] RIGHT,
  input  INPUT_VALID,
  output [15:0] RESULT,
  output RESULT_VALID
);

  wire [15:0] BITWISE_AND_out;

  assign BITWISE_AND_out = LEFT & RIGHT;  // AND_Gate BITWISE_AND, 16 bits wide
  Multiplexer #(.width(16)) multiplexer_1 (.in0({16{1'b0}}), .in1(BITWISE_AND_out), .out(RESULT), .sel(AND_ACTIVATED));
  and ACTIVE_AND_VALID (RESULT_VALID, AND_ACTIVATED, INPUT_VALID);

  // Notes on the sheet:
  //   bitwise AND: inactive outputs are neutral
endmodule

module Operations (
  input  [15:0] ACC_VALUE,
  input  [15:0] MEMORY_VALUE,
  input  [15:0] IMMEDIATE_VALUE,
  input  MEMORY_VALID,
  input  ACC_VALID,
  input  CONST_OPERAND,
  input  ADD_OPERAND,
  input  SUB_OPERAND,
  input  MUL_OPERAND,
  input  DIV_OPERAND,
  input  AND_OPERAND,
  input  OR_OPERAND,
  input  XOR_OPERAND,
  input  NOT_OPERAND,
  output [15:0] RESULT_VALUE,
  output OVERFLOW,
  output RESULT_IS_VALID,
  output INVALID_OPERAND,
  output DIVIDE_BY_ZERO
);

  wire ACC_ADD_VALID_out, ADD_OPERATION_overflow, ADD_OPERATION_result_valid, AND_OPERATION_result_valid,
       DIV_OPERATION_result_valid, MUL_OPERATION_overflow, MUL_OPERATION_result_valid, multiplexer_1_out,
       not_1_out, NOT_OPERATION_result_valid, OPERATION_IS_ACTIVE_out, OPERATION_RESULT_VALID_out,
       OR_OPERATION_result_valid, SUB_OPERATION_overflow, SUB_OPERATION_result_valid,
       XOR_OPERATION_result_valid;
  wire [15:0] ADD_OPERATION_result, AND_OPERATION_result, DIV_OPERATION_result, MUL_OPERATION_result,
       multiplexer_2_out, NOT_OPERATION_result, OR_OPERATION_result, RESULT_out, SUB_OPERATION_result,
       XOR_OPERATION_result;

  Multiplexer multiplexer_1 (.in0(MEMORY_VALID), .in1(1'b1), .out(multiplexer_1_out), .sel(CONST_OPERAND));
  Multiplexer #(.width(16)) multiplexer_2 (
    .in0(MEMORY_VALUE), .in1(IMMEDIATE_VALUE), .out(multiplexer_2_out), .sel(CONST_OPERAND));
  and ACC_ADD_VALID (ACC_ADD_VALID_out, multiplexer_1_out, ACC_VALID);
  AddArithmeticCircuit ADD_OPERATION (
    .ADD_ACTIVATED(ADD_OPERAND), .LEFT(ACC_VALUE), .RIGHT(multiplexer_2_out),
    .INPUT_VALID(ACC_ADD_VALID_out), .RESULT(ADD_OPERATION_result), .OVERFLOW(ADD_OPERATION_overflow),
    .RESULT_VALID(ADD_OPERATION_result_valid));
  SubArithmeticCircuit SUB_OPERATION (
    .SUB_ACTIVATED(SUB_OPERAND), .LEFT(ACC_VALUE), .RIGHT(multiplexer_2_out),
    .INPUT_VALID(ACC_ADD_VALID_out), .RESULT(SUB_OPERATION_result), .OVERFLOW(SUB_OPERATION_overflow),
    .RESULT_VALID(SUB_OPERATION_result_valid));
  MulArithmeticCircuit MUL_OPERATION (
    .MUL_ACTIVATED(MUL_OPERAND), .LEFT(ACC_VALUE), .RIGHT(multiplexer_2_out),
    .INPUT_VALID(ACC_ADD_VALID_out), .RESULT(MUL_OPERATION_result), .OVERFLOW(MUL_OPERATION_overflow),
    .RESULT_VALID(MUL_OPERATION_result_valid));
  DivArithmeticCircuit DIV_OPERATION (
    .DIV_ACTIVATED(DIV_OPERAND), .LEFT(ACC_VALUE), .RIGHT(multiplexer_2_out),
    .INPUT_VALID(ACC_ADD_VALID_out), .RESULT(DIV_OPERATION_result),
    .RESULT_VALID(DIV_OPERATION_result_valid), .DIVIDE_BY_ZERO(DIVIDE_BY_ZERO));
  AndArithmeticCircuit AND_OPERATION (
    .AND_ACTIVATED(AND_OPERAND), .LEFT(ACC_VALUE), .RIGHT(multiplexer_2_out),
    .INPUT_VALID(ACC_ADD_VALID_out), .RESULT(AND_OPERATION_result), .RESULT_VALID(AND_OPERATION_result_valid));
  OrArithmeticCircuit OR_OPERATION (
    .OR_ACTIVATED(OR_OPERAND), .LEFT(ACC_VALUE), .RIGHT(multiplexer_2_out), .INPUT_VALID(ACC_ADD_VALID_out),
    .RESULT(OR_OPERATION_result), .RESULT_VALID(OR_OPERATION_result_valid));
  XorArithmeticCircuit XOR_OPERATION (
    .XOR_ACTIVATED(XOR_OPERAND), .LEFT(ACC_VALUE), .RIGHT(multiplexer_2_out),
    .INPUT_VALID(ACC_ADD_VALID_out), .RESULT(XOR_OPERATION_result), .RESULT_VALID(XOR_OPERATION_result_valid));
  NotCircuit NOT_OPERATION (
    .NOT_IS_ACTIVE(NOT_OPERAND), .ACC_VALUE(ACC_VALUE), .ACC_VALID(ACC_ADD_VALID_out),
    .RESULT(NOT_OPERATION_result), .RESULT_VALID(NOT_OPERATION_result_valid));
  assign RESULT_out = ADD_OPERATION_result | SUB_OPERATION_result | MUL_OPERATION_result | DIV_OPERATION_result | AND_OPERATION_result | OR_OPERATION_result | XOR_OPERATION_result | NOT_OPERATION_result;  // OR_Gate RESULT, 16 bits wide
  or OVERFLOW_SET (OVERFLOW, ADD_OPERATION_overflow, SUB_OPERATION_overflow, MUL_OPERATION_overflow);
  or OPERATION_RESULT_VALID (OPERATION_RESULT_VALID_out, ADD_OPERATION_result_valid, SUB_OPERATION_result_valid, MUL_OPERATION_result_valid, DIV_OPERATION_result_valid, AND_OPERATION_result_valid, OR_OPERATION_result_valid, XOR_OPERATION_result_valid, NOT_OPERATION_result_valid);
  or OPERATION_IS_ACTIVE (OPERATION_IS_ACTIVE_out, ADD_OPERAND, SUB_OPERAND, MUL_OPERAND, DIV_OPERAND, AND_OPERAND, OR_OPERAND, XOR_OPERAND, NOT_OPERAND);
  not not_1 (not_1_out, OPERATION_RESULT_VALID_out);
  Multiplexer #(.width(16)) multiplexer_3 (
    .in0(multiplexer_2_out), .in1(RESULT_out), .out(RESULT_VALUE), .sel(OPERATION_IS_ACTIVE_out));
  Multiplexer multiplexer_4 (
    .in0(ACC_ADD_VALID_out), .in1(OPERATION_RESULT_VALID_out), .out(RESULT_IS_VALID),
    .sel(OPERATION_IS_ACTIVE_out));
  and ACTIVE_INVALID_OPERATION (INVALID_OPERAND, not_1_out, OPERATION_IS_ACTIVE_out);
endmodule

module NotCircuit (
  input  NOT_IS_ACTIVE,
  input  [15:0] ACC_VALUE,
  input  ACC_VALID,
  output [15:0] RESULT,
  output RESULT_VALID
);

  wire [15:0] NOT_VALUE_out;

  assign NOT_VALUE_out = ~ACC_VALUE;  // NOT_Gate NOT_VALUE, 16 bits wide
  Multiplexer #(.width(16)) multiplexer_1 (.in0({16{1'b0}}), .in1(NOT_VALUE_out), .out(RESULT), .sel(NOT_IS_ACTIVE));
  and ACTIVE_NOT_VALID (RESULT_VALID, ACC_VALID, NOT_IS_ACTIVE);
endmodule

module MulArithmeticCircuit (
  input  MUL_ACTIVATED,
  input  [15:0] LEFT,
  input  [15:0] RIGHT,
  input  INPUT_VALID,
  output [15:0] RESULT,
  output OVERFLOW,
  output RESULT_VALID
);

  wire NO_OVERFLOW_out, OPERAND_SIGN_DIFFERENT_out, RESULT_SIGN_CHANGED_out;
  wire [14:0] multiplexer_2_out;
  wire [15:0] multiplexer_1_out;
  wire [15:15] multiplexer_2_out_2;

  Multiplexer #(.width(16)) multiplexer_1 (.in0({16{1'b0}}), .in1(LEFT), .out(multiplexer_1_out), .sel(MUL_ACTIVATED));
  Multiplexer #(.width(16)) multiplexer_2 (
    .in0({16{1'b0}}), .in1(RIGHT), .out({multiplexer_2_out_2[15], multiplexer_2_out}), .sel(MUL_ACTIVATED));
  Multiplier #(.width(16)) multiplier_1 (
    .a(multiplexer_1_out), .b({multiplexer_2_out_2[15], multiplexer_2_out}), .out(RESULT));  // open: cin, cout
  xor OPERAND_SIGN_DIFFERENT (OPERAND_SIGN_DIFFERENT_out, multiplexer_1_out[15], multiplexer_2_out_2[15]);
  xor RESULT_SIGN_CHANGED (RESULT_SIGN_CHANGED_out, RESULT[15], multiplexer_1_out[15]);
  not NO_OVERFLOW (NO_OVERFLOW_out, OPERAND_SIGN_DIFFERENT_out);
  and SIGN_OVERFLOW (OVERFLOW, RESULT_SIGN_CHANGED_out, OPERAND_SIGN_DIFFERENT_out);
  and RANGE_VALID (RESULT_VALID, NO_OVERFLOW_out, INPUT_VALID);

  // Notes on the sheet:
  //   signed MUL: overflow = (left_sign XOR right_sign) AND (left_sign XOR result_sign)
endmodule

module DivArithmeticCircuit (
  input  DIV_ACTIVATED,
  input  [15:0] LEFT,
  input  [15:0] RIGHT,
  input  INPUT_VALID,
  output [15:0] RESULT,
  output RESULT_VALID,
  output DIVIDE_BY_ZERO
);

  wire comparator_1_gt, NONZERO_DIVISOR_out;
  wire [15:0] multiplexer_1_out, multiplexer_2_out;

  Multiplexer #(.width(16)) multiplexer_1 (.in0({16{1'b0}}), .in1(LEFT), .out(multiplexer_1_out), .sel(DIV_ACTIVATED));
  Multiplexer #(.width(16)) multiplexer_2 (.in0(16'h1), .in1(RIGHT), .out(multiplexer_2_out), .sel(DIV_ACTIVATED));
  Divider #(.mode("twosComplement"), .width(16)) divider_1 (
    .a(multiplexer_1_out), .b(multiplexer_2_out), .out(RESULT));  // open: upper, rem
  Comparator #(.width(16)) comparator_1 (.a(multiplexer_2_out), .b(16'h1), .gt(comparator_1_gt));  // open: eq, lt
  not NONZERO_DIVISOR (NONZERO_DIVISOR_out, comparator_1_gt);
  and RANGE_VALID (RESULT_VALID, comparator_1_gt, DIV_ACTIVATED, INPUT_VALID);
  and DIVIDE_BY_ZERO_ACTIVE (DIVIDE_BY_ZERO, NONZERO_DIVISOR_out, DIV_ACTIVATED);
endmodule

module AddArithmeticCircuit (
  input  ADD_ACTIVATED,
  input  [15:0] LEFT,
  input  [15:0] RIGHT,
  input  INPUT_VALID,
  output [15:0] RESULT,
  output OVERFLOW,
  output RESULT_VALID
);

  wire NO_OVERFLOW_out, OPERAND_SIGN_DIFFERENT_out, OPERAND_SIGN_SAME_out, RESULT_SIGN_CHANGED_out;
  wire [14:0] multiplexer_2_out;
  wire [15:0] multiplexer_1_out;
  wire [15:15] multiplexer_2_out_2;

  Multiplexer #(.width(16)) multiplexer_1 (.in0({16{1'b0}}), .in1(LEFT), .out(multiplexer_1_out), .sel(ADD_ACTIVATED));
  Multiplexer #(.width(16)) multiplexer_2 (
    .in0({16{1'b0}}), .in1(RIGHT), .out({multiplexer_2_out_2[15], multiplexer_2_out}), .sel(ADD_ACTIVATED));
  Adder #(.width(16)) adder_1 (
    .a(multiplexer_1_out), .b({multiplexer_2_out_2[15], multiplexer_2_out}), .out(RESULT));  // open: cin, cout
  xor OPERAND_SIGN_DIFFERENT (OPERAND_SIGN_DIFFERENT_out, multiplexer_1_out[15], multiplexer_2_out_2[15]);
  not OPERAND_SIGN_SAME (OPERAND_SIGN_SAME_out, OPERAND_SIGN_DIFFERENT_out);
  xor RESULT_SIGN_CHANGED (RESULT_SIGN_CHANGED_out, RESULT[15], multiplexer_1_out[15]);
  not NO_OVERFLOW (NO_OVERFLOW_out, OPERAND_SIGN_SAME_out);
  and SIGN_OVERFLOW (OVERFLOW, RESULT_SIGN_CHANGED_out, OPERAND_SIGN_SAME_out);
  and RANGE_VALID (RESULT_VALID, NO_OVERFLOW_out, ADD_ACTIVATED, INPUT_VALID);

  // Notes on the sheet:
  //   signed ADD: overflow = NOT(left_sign XOR right_sign) AND (left_sign XOR result_sign)
endmodule

module SubArithmeticCircuit (
  input  SUB_ACTIVATED,
  input  [15:0] LEFT,
  input  [15:0] RIGHT,
  input  INPUT_VALID,
  output [15:0] RESULT,
  output OVERFLOW,
  output RESULT_VALID
);

  wire NO_OVERFLOW_out, OPERAND_SIGN_DIFFERENT_out, RESULT_SIGN_CHANGED_out;
  wire [14:0] multiplexer_2_out;
  wire [15:0] multiplexer_1_out;
  wire [15:15] multiplexer_2_out_2;

  Multiplexer #(.width(16)) multiplexer_1 (.in0({16{1'b0}}), .in1(LEFT), .out(multiplexer_1_out), .sel(SUB_ACTIVATED));
  Multiplexer #(.width(16)) multiplexer_2 (
    .in0({16{1'b0}}), .in1(RIGHT), .out({multiplexer_2_out_2[15], multiplexer_2_out}), .sel(SUB_ACTIVATED));
  Subtractor #(.width(16)) subtractor_1 (
    .a(multiplexer_1_out), .b({multiplexer_2_out_2[15], multiplexer_2_out}), .out(RESULT));  // open: bin, bout
  xor OPERAND_SIGN_DIFFERENT (OPERAND_SIGN_DIFFERENT_out, multiplexer_1_out[15], multiplexer_2_out_2[15]);
  xor RESULT_SIGN_CHANGED (RESULT_SIGN_CHANGED_out, RESULT[15], multiplexer_1_out[15]);
  not NO_OVERFLOW (NO_OVERFLOW_out, OPERAND_SIGN_DIFFERENT_out);
  and SIGN_OVERFLOW (OVERFLOW, RESULT_SIGN_CHANGED_out, OPERAND_SIGN_DIFFERENT_out);
  and RANGE_VALID (RESULT_VALID, NO_OVERFLOW_out, SUB_ACTIVATED, INPUT_VALID);

  // Notes on the sheet:
  //   signed SUB: overflow = (left_sign XOR right_sign) AND (left_sign XOR result_sign)
endmodule

module AddressRangeFBox (
  input  OFFSET_CARRY,
  input  EFFECTIVE_REGISTER_MODE,
  input  EFFECTIVE_OFFSET_MODE,
  input  ADDRESS_OUT_OF_RANGE,
  input  ADDRESS_OPERAND,
  output ACTIVE_ADDRESS_OUT_OF_RANGE
);

  wire ACTIVE_ADDRESS_RANGE_GATE_out, ACTIVE_OFFSET_ADDRESS_ERROR_out, MEMORY_ADDRESS_ACTIVE_out;

  or MEMORY_ADDRESS_ACTIVE (MEMORY_ADDRESS_ACTIVE_out, ADDRESS_OPERAND, EFFECTIVE_REGISTER_MODE, EFFECTIVE_OFFSET_MODE);
  and ACTIVE_ADDRESS_RANGE_GATE (ACTIVE_ADDRESS_RANGE_GATE_out, MEMORY_ADDRESS_ACTIVE_out, ADDRESS_OUT_OF_RANGE);
  and ACTIVE_OFFSET_ADDRESS_ERROR (ACTIVE_OFFSET_ADDRESS_ERROR_out, OFFSET_CARRY, EFFECTIVE_OFFSET_MODE);
  or ACTIVE_ADDRESS_ERROR (ACTIVE_ADDRESS_OUT_OF_RANGE, ACTIVE_OFFSET_ADDRESS_ERROR_out, ACTIVE_ADDRESS_RANGE_GATE_out);
endmodule

module OrArithmeticCircuit (
  input  OR_ACTIVATED,
  input  [15:0] LEFT,
  input  [15:0] RIGHT,
  input  INPUT_VALID,
  output [15:0] RESULT,
  output RESULT_VALID
);

  wire [15:0] BITWISE_OR_out;

  assign BITWISE_OR_out = LEFT | RIGHT;  // OR_Gate BITWISE_OR, 16 bits wide
  Multiplexer #(.width(16)) multiplexer_1 (.in0({16{1'b0}}), .in1(BITWISE_OR_out), .out(RESULT), .sel(OR_ACTIVATED));
  and ACTIVE_OR_VALID (RESULT_VALID, OR_ACTIVATED, INPUT_VALID);

  // Notes on the sheet:
  //   bitwise OR: inactive outputs are neutral
endmodule

module XorArithmeticCircuit (
  input  XOR_ACTIVATED,
  input  [15:0] LEFT,
  input  [15:0] RIGHT,
  input  INPUT_VALID,
  output [15:0] RESULT,
  output RESULT_VALID
);

  wire [15:0] BITWISE_XOR_out;

  assign BITWISE_XOR_out = LEFT ^ RIGHT;  // XOR_Gate BITWISE_XOR, 16 bits wide
  Multiplexer #(.width(16)) multiplexer_1 (.in0({16{1'b0}}), .in1(BITWISE_XOR_out), .out(RESULT), .sel(XOR_ACTIVATED));
  and ACTIVE_XOR_VALID (RESULT_VALID, XOR_ACTIVATED, INPUT_VALID);

  // Notes on the sheet:
  //   bitwise XOR: inactive outputs are neutral
endmodule

module JumpBox (
  input  ERROR_OVF,
  input  ERROR_DIV0,
  input  ERROR_ADDR,
  input  ERROR_INV,
  input  ERROR_ILL,
  input  ERROR_INPUT,
  input  JUMP_ADR,
  input  JUMP_ZERO,
  input  JUMP_NOT_ZERO,
  input  JUMP_NEGATIVE,
  input  JUMP_ERROR,
  input  JUMP_NOT_ERROR,
  input  NEGATIVE,
  input  ZERO,
  output IS_NOT_ZERO,
  output DEC_JUMP_NOT_ZERO
);

  wire ANY_ERROR_FOR_JUMP_out, INVERT_ANY_ERROR_FOR_JUMP_NOT_ERROR_out, INVERT_ZERO_FOR_JZ_out,
       JUMP_ADR_OR_JNZ_CONTROL_out, JUMP_ADR_OR_NOT_ZERO_out, JUMP_ERROR_AND_ANY_ERROR_out,
       JUMP_ERROR_OR_PREVIOUS_CONTROLS_out, JUMP_ERROR_OR_PREVIOUS_TAKEN_out, JUMP_NEGATIVE_AND_NEGATIVE_out,
       JUMP_NEGATIVE_OR_PREVIOUS_CONTROLS_out, JUMP_NEGATIVE_OR_PREVIOUS_TAKEN_out,
       JUMP_NOT_ERROR_AND_NO_ERROR_out, JUMP_ZERO_AND_ZERO_out, JUMP_ZERO_OR_PREVIOUS_CONTROLS_out,
       JUMP_ZERO_OR_PREVIOUS_TAKEN_out;

  or ANY_ERROR_FOR_JUMP (ANY_ERROR_FOR_JUMP_out, ERROR_OVF, ERROR_DIV0, ERROR_ADDR, ERROR_INV, ERROR_ILL, ERROR_INPUT);
  or JUMP_ADR_OR_JNZ_CONTROL (JUMP_ADR_OR_JNZ_CONTROL_out, JUMP_NOT_ZERO, JUMP_ADR);
  not INVERT_ZERO_FOR_JZ (INVERT_ZERO_FOR_JZ_out, ZERO);
  or JUMP_ZERO_OR_PREVIOUS_CONTROLS (JUMP_ZERO_OR_PREVIOUS_CONTROLS_out, JUMP_ADR_OR_JNZ_CONTROL_out, JUMP_ZERO);
  or JUMP_ADR_OR_NOT_ZERO (JUMP_ADR_OR_NOT_ZERO_out, JUMP_ADR, ZERO);
  and JUMP_ZERO_AND_ZERO (JUMP_ZERO_AND_ZERO_out, JUMP_ZERO, INVERT_ZERO_FOR_JZ_out);
  and JUMP_NEGATIVE_AND_NEGATIVE (JUMP_NEGATIVE_AND_NEGATIVE_out, JUMP_NEGATIVE, NEGATIVE);
  or JUMP_NEGATIVE_OR_PREVIOUS_CONTROLS (JUMP_NEGATIVE_OR_PREVIOUS_CONTROLS_out, JUMP_ZERO_OR_PREVIOUS_CONTROLS_out, JUMP_NEGATIVE);
  or JUMP_ZERO_OR_PREVIOUS_TAKEN (JUMP_ZERO_OR_PREVIOUS_TAKEN_out, JUMP_ADR_OR_NOT_ZERO_out, JUMP_ZERO_AND_ZERO_out);
  or JUMP_NEGATIVE_OR_PREVIOUS_TAKEN (JUMP_NEGATIVE_OR_PREVIOUS_TAKEN_out, JUMP_ZERO_OR_PREVIOUS_TAKEN_out, JUMP_NEGATIVE_AND_NEGATIVE_out);
  and JUMP_ERROR_AND_ANY_ERROR (JUMP_ERROR_AND_ANY_ERROR_out, JUMP_NOT_ERROR, ANY_ERROR_FOR_JUMP_out);
  not INVERT_ANY_ERROR_FOR_JUMP_NOT_ERROR (INVERT_ANY_ERROR_FOR_JUMP_NOT_ERROR_out, ANY_ERROR_FOR_JUMP_out);
  or JUMP_ERROR_OR_PREVIOUS_CONTROLS (JUMP_ERROR_OR_PREVIOUS_CONTROLS_out, JUMP_NOT_ERROR, JUMP_NEGATIVE_OR_PREVIOUS_CONTROLS_out);
  or JUMP_ERROR_OR_PREVIOUS_TAKEN (JUMP_ERROR_OR_PREVIOUS_TAKEN_out, JUMP_NEGATIVE_OR_PREVIOUS_TAKEN_out, JUMP_ERROR_AND_ANY_ERROR_out);
  and JUMP_NOT_ERROR_AND_NO_ERROR (JUMP_NOT_ERROR_AND_NO_ERROR_out, JUMP_ERROR, INVERT_ANY_ERROR_FOR_JUMP_NOT_ERROR_out);
  or JUMP_NOT_ERROR_OR_PREVIOUS_CONTROLS (IS_NOT_ZERO, JUMP_ERROR_OR_PREVIOUS_CONTROLS_out, JUMP_ERROR);
  or JUMP_NOT_ERROR_OR_PREVIOUS_TAKEN (DEC_JUMP_NOT_ZERO, JUMP_ERROR_OR_PREVIOUS_TAKEN_out, JUMP_NOT_ERROR_AND_NO_ERROR_out);
endmodule
