// Logisim project TinyCPU_Peripherals.circ as structural Verilog: 4 circuits, main circuit TinyCPUSystemMain
module TinyCPUSystemMain (
  input  CLK,
  input  RESET,
  input  INTERRUPT_REQUEST,
  output [15:0] OUTPUT_PORT_VALUE,
  output OUTPUT_PORT_VALID,
  output INTERRUPT_ENABLED,
  output INTERRUPT_PENDING,
  output IN_INTERRUPT_HANDLER,
  output [11:0] RETURN_ADDRESS,
  output RETURN_ADDRESS_VALID
);
endmodule

module OutputPort (
  input  [15:0] WRITE_VALUE,
  input  WRITE_VALID,
  input  WRITE_ENABLE,
  input  CLK,
  input  RESET,
  output [15:0] VALUE,
  output VALID
);

  wire OUTPUT_WRITE_ACCEPTED_out;

  buf OUTPUT_WRITE_ACCEPTED (OUTPUT_WRITE_ACCEPTED_out, WRITE_VALID);  // AND_Gate
  Register #(.width(16)) OUTPUT_VALUE (
    .D(WRITE_VALUE), .en(OUTPUT_WRITE_ACCEPTED_out), .clk(CLK), .Q(VALUE), .clr(RESET));
  Register #(.width(1)) OUTPUT_VALID (
    .D(WRITE_VALID), .en(OUTPUT_WRITE_ACCEPTED_out), .clk(CLK), .Q(VALID), .clr(RESET));
endmodule

module OutputMemoryPath (
  input  [11:0] ADDRESS,
  input  [15:0] WRITE_VALUE,
  input  WRITE_VALID,
  input  WRITE_ENABLE,
  input  [15:0] RAM_READ_VALUE,
  input  RAM_READ_VALID,
  input  CLK,
  input  RESET,
  output [15:0] READ_VALUE,
  output READ_VALID,
  output RAM_WRITE_ENABLE,
  output [15:0] OUTPUT_PORT_VALUE,
  output OUTPUT_PORT_VALID
);

  wire NOT_OUTPUT_ADDRESS_out, OUTPUT_WRITE_GATE_out, RAM_WRITE_GATE_p2, RAM_WRITE_GATE_p4,
       RAM_WRITE_GATE_p6, undriven_2, undriven_3, undriven_4;
  wire [11:0] undriven;

  Comparator #(.width(12)) OUTPUT_ADDRESS_DECODE (.a(undriven), .b(ADDRESS));  // open: gt, eq, lt
  not NOT_OUTPUT_ADDRESS (NOT_OUTPUT_ADDRESS_out, undriven_2);
  // AND_Gate RAM_WRITE_GATE: pin names not known; wires that end beside it: WRITE_ENABLE, RAM_WRITE_GATE_p2, NOT_OUTPUT_ADDRESS_out, RAM_WRITE_GATE_p4, RAM_WRITE_GATE_p4, RAM_WRITE_GATE_p6, RAM_WRITE_ENABLE
  buf OUTPUT_WRITE_GATE (OUTPUT_WRITE_GATE_out, RAM_WRITE_GATE_p2);  // AND_Gate
  Multiplexer #(.width(16)) OUTPUT_READ_VALUE_SELECT (
    .in0(RAM_READ_VALUE), .in1(OUTPUT_PORT_VALUE), .out(READ_VALUE));  // open: sel
  Multiplexer OUTPUT_READ_VALID_SELECT (.in0(RAM_READ_VALID), .in1(OUTPUT_PORT_VALID), .out(READ_VALID));  // open: sel
  Register #(.width(16)) u_OUTPUT_PORT_VALUE (
    .D(WRITE_VALUE), .clk(undriven_3), .Q(OUTPUT_PORT_VALUE), .clr(undriven_4));  // open: en
  Register #(.width(1)) u_OUTPUT_PORT_VALID (
    .D(WRITE_VALID), .en(OUTPUT_WRITE_GATE_out), .clk(undriven_3), .Q(OUTPUT_PORT_VALID), .clr(undriven_4));
endmodule

module InterruptController (
  input  INTERRUPT_REQUEST,
  input  INSTRUCTION_BOUNDARY,
  input  ENABLE_REQUEST,
  input  DISABLE_REQUEST,
  input  RETURN_REQUEST,
  input  [11:0] NEXT_PC,
  input  CLK,
  input  RESET,
  output INTERRUPT_ACCEPT,
  output [11:0] TARGET_PC,
  output INTERRUPT_ENABLED,
  output INTERRUPT_PENDING,
  output IN_INTERRUPT_HANDLER,
  output [11:0] RETURN_ADDRESS,
  output RETURN_ADDRESS_VALID,
  output ILLEGAL_RETURN
);

  wire HANDLER_HOLD_out, INTERRUPT_ACCEPT_GATE_p3, INTERRUPT_ENABLED_p1, INTERRUPT_PENDING_p3,
       INTERRUPT_PENDING_p4, INTERRUPT_TARGET_SELECT_p1, INTERRUPT_TARGET_SELECT_p3, MASK_CLEAR_NOT_out,
       MASK_CLEAR_REQUEST_p4, MASK_HOLD_p3, MASK_SET_REQUEST_out, NOT_IN_HANDLER_out,
       PENDING_HOLD_UNTIL_ACCEPT_p4, PENDING_HOLD_UNTIL_ACCEPT_p5, PENDING_HOLD_UNTIL_ACCEPT_p6,
       PENDING_SET_OR_HOLD_out, PREVIOUS_REQUEST_NOT_out, REQUEST_LEVEL_q, RETURN_VALID_HOLD_p1,
       RETURN_VALID_HOLD_p2, RETURN_VALID_NEXT_p1, RISING_EDGE_DETECT_out, undriven, undriven_2,
       VALID_RETURN_GATE_out, VALID_RETURN_NOT_out;

  or PENDING_SET_OR_HOLD (PENDING_SET_OR_HOLD_out, DISABLE_REQUEST, RETURN_REQUEST);
  // OR_Gate MASK_SET_REQUEST has open pins: out=MASK_SET_REQUEST_out
  // OR_Gate MASK_CLEAR_REQUEST: pin names not known; wires that end beside it: RETURN_REQUEST, DISABLE_REQUEST, INTERRUPT_ACCEPT, MASK_CLEAR_REQUEST_p4
  Register #(.width(1)) REQUEST_LEVEL (.D(INTERRUPT_REQUEST), .en(1'b1), .clk(CLK), .Q(REQUEST_LEVEL_q), .clr(RESET));
  // Register #(.width(1)) INTERRUPT_ENABLED: pin names not known; wires that end beside it: INTERRUPT_ENABLED_p1, 1'b1, CLK, RESET
  // Register #(.width(1)) INTERRUPT_PENDING: pin names not known; wires that end beside it: PENDING_SET_OR_HOLD_out, 1'b1, INTERRUPT_PENDING_p3, INTERRUPT_PENDING_p4, RESET, INTERRUPT_PENDING
  Register #(.width(1)) u_IN_INTERRUPT_HANDLER (
    .D(INTERRUPT_PENDING_p4), .en(PENDING_HOLD_UNTIL_ACCEPT_p6), .clk(CLK), .Q(IN_INTERRUPT_HANDLER),
    .clr(RESET));
  Register #(.width(12)) u_RETURN_ADDRESS (
    .D(NEXT_PC), .en(INTERRUPT_ACCEPT), .clk(CLK), .Q(RETURN_ADDRESS), .clr(RESET));
  // Register #(.width(1)) RETURN_ADDRESS_VALID: pin names not known; wires that end beside it: CLK, RESET, RETURN_ADDRESS_VALID
  // NOT_Gate MASK_CLEAR_NOT has open pins: in=open, out=MASK_CLEAR_NOT_out
  not PREVIOUS_REQUEST_NOT (PREVIOUS_REQUEST_NOT_out, REQUEST_LEVEL_q);
  not NOT_IN_HANDLER (NOT_IN_HANDLER_out, IN_INTERRUPT_HANDLER);
  // AND_Gate MASK_HOLD: pin names not known; wires that end beside it: RESET, MASK_CLEAR_NOT_out, MASK_HOLD_p3, MASK_SET_REQUEST_out
  buf RISING_EDGE_DETECT (RISING_EDGE_DETECT_out, PREVIOUS_REQUEST_NOT_out);  // AND_Gate
  // AND_Gate INTERRUPT_ACCEPT_GATE: pin names not known; wires that end beside it: RESET, INSTRUCTION_BOUNDARY, INTERRUPT_ACCEPT_GATE_p3, NOT_IN_HANDLER_out, INTERRUPT_ACCEPT
  // AND_Gate ILLEGAL_RETURN_GATE is placed but not wired
  // AND_Gate PENDING_HOLD_UNTIL_ACCEPT: pin names not known; wires that end beside it: INTERRUPT_PENDING, NOT_IN_HANDLER_out, INTERRUPT_ACCEPT_GATE_p3, PENDING_HOLD_UNTIL_ACCEPT_p4, PENDING_HOLD_UNTIL_ACCEPT_p5, PENDING_HOLD_UNTIL_ACCEPT_p6
  // OR_Gate MASK_NEXT has open pins: out=INTERRUPT_ENABLED_p1
  and VALID_RETURN_GATE (VALID_RETURN_GATE_out, undriven, undriven_2);
  // AND_Gate RETURN_VALID_HOLD: pin names not known; wires that end beside it: RETURN_VALID_HOLD_p1, RETURN_VALID_HOLD_p2
  // AND_Gate HANDLER_HOLD has open pins: out=HANDLER_HOLD_out
  not INTERRUPT_ACCEPT_NOT (PENDING_HOLD_UNTIL_ACCEPT_p4, INTERRUPT_ACCEPT);
  // Multiplexer #(.width(12)) INTERRUPT_TARGET_SELECT: pin names not known; wires that end beside it: INTERRUPT_TARGET_SELECT_p1, RETURN_ADDRESS, INTERRUPT_TARGET_SELECT_p3, INTERRUPT_TARGET_SELECT_p3, TARGET_PC
  not VALID_RETURN_NOT (VALID_RETURN_NOT_out, VALID_RETURN_GATE_out);
  // OR_Gate RETURN_VALID_NEXT: pin names not known; wires that end beside it: RETURN_VALID_NEXT_p1
  // OR_Gate HANDLER_NEXT: pin names not known; wires that end beside it: INTERRUPT_ACCEPT, HANDLER_HOLD_out

  assign INTERRUPT_ENABLED = RESET;
endmodule
